// Digital circuit HD3112_BCD_Adder_Subtractor_1.dig as structural Verilog
module HD3112_BCD_Adder_Subtractor_1 (
  input  A,
  input  B,
  input  SUB,
  input  clk,
  input  in_9,
  input  in_10,
  output out_1,
  output out_2,
  output out_3,
  output out_4,
  output out_11,
  output out_12
);

  wire and_1_out, and_2_out, and_3_out, and_4_out, and_5_out, and_6_out, and_7_out, and_8_out, and_9_out, CF,
       CY, d_ff_6_q, d_ff_7_q, d_ff_8_q, nB8, not_2_out, or_1_out, or_2_out, or_3_out, or_5_out, or_6_out,
       Q0, xor_1_out, xor_2_out, xor_4_out, xor_5_out;

  xor xor_1 (xor_1_out, SUB, B);
  or or_1 (or_1_out, SUB, CF);
  xor xor_2 (xor_2_out, A, B);
  and and_1 (and_1_out, xor_1_out, or_1_out);
  and and_2 (and_2_out, SUB, CF);
  xor xor_3 (out_1, xor_2_out, CF);
  or or_2 (or_2_out, and_1_out, and_2_out);
  D_FF d_ff_1 (.D(out_1), .C(clk), .Q(out_2));  // open: nQ
  or or_3 (or_3_out, out_3, out_2);
  D_FF d_ff_2 (.D(out_2), .C(clk), .Q(out_3));  // open: nQ
  not not_1 (nB8, in_9);
  and and_3 (and_3_out, or_3_out, out_1, in_9);
  D_FF d_ff_3 (.D(out_3), .C(clk), .Q(out_4));  // open: nQ
  or or_4 (CY, and_3_out, or_2_out);
  not not_2 (not_2_out, in_10);
  D_FF d_ff_4 (.D(out_4), .C(clk), .Q(Q0));  // open: nQ
  and and_4 (and_4_out, CY, not_2_out);
  D_FF d_ff_5 (.D(and_4_out), .C(clk), .Q(CF));  // open: nQ
  D_FF d_ff_6 (.D(in_9), .C(clk), .Q(d_ff_6_q));  // open: nQ
  and and_5 (and_5_out, CF, d_ff_6_q);
  or or_5 (or_5_out, and_7_out, and_5_out);
  D_FF d_ff_7 (.D(or_5_out), .C(clk), .Q(d_ff_7_q));  // open: nQ
  and and_6 (and_6_out, in_9, clk);
  and and_7 (and_7_out, d_ff_7_q, nB8);
  D_FF d_ff_8 (.D(SUB), .C(and_6_out), .Q(d_ff_8_q));  // open: nQ
  xor xor_4 (xor_4_out, Q0, and_7_out);
  xor xor_5 (xor_5_out, d_ff_8_q, Q0);
  and and_8 (and_8_out, xor_5_out, and_7_out);
  and and_9 (and_9_out, out_12, nB8);
  xor xor_6 (out_11, xor_4_out, out_12);
  or or_6 (or_6_out, and_8_out, and_9_out);
  D_FF d_ff_9 (.D(or_6_out), .C(clk), .Q(out_12));  // open: nQ

  // Other names for the same wires on the sheet: B8 = in_9; Cout = out_12; DE_B8 = in_10; Q1 = out_4; Q2 = out_3;
  //   Q3 = out_2; Q4 = out_1; SUM = out_11

  // Notes on the sheet:
  //   Operand Adder
  //   Tens Carry
  //   Carry
  //   Flag
  //   SIX Generator
  //   Normalisation Adder
  //   Normalisation
  //   Carry Flag
endmodule
